# Fritzing sketch Schéma (saved by Fritzing 0.9.3b)
circuit board: 8.46667cm x 5.64444cm
perfboards: 1

parts:
  U1 = atmega328 [package=dip]
  LED1 = LED - 5mm [color="Red (635nm)" package="5 mm [THT]"]
  J1 = male pin header, 4 pins [form="♂ (male)"]
  J2 = male pin header, 15 pins [form="♂ (male)"]
  R1 = Resistor [tolerance=±5% resistance=1k package=THT]
  C1 = Electrolytic Capacitor [capacitance=1µF package="100 mil [THT, electrolytic]"]
  R2 = Resistor [tolerance=±5% resistance=10k package=THT]
  J3 = male pin header, 5 pins [form="♂ (male)"]
  J4 = male pin header, 5 pins [form="♂ (male)"]
  U2 = AD22100 - Voltage Output Temperature Sensor with Signal Conditioning [part_number=AD22100]

nets:
  Reset: U1.RESET, R2.Pin_1, J3.pin3
  Cniv3: U1.D2, J2.pin11
  Cniv10: U1.D3_(PWM), J2.pin10
  Cniv20: U1.D4, J2.pin9
  5V: U1.VCC, U1.AVCC, LED1.anode, J1.pin1, J2.pin13, C1.+, R2.Pin_0, J4.pin1, U2.V+
  GND: U1.GND, J1.pin4, J2.pin12, J2.pin15, C1.-, J4.pin5, U2.GND
  Cniv30: U1.D5_(PWM), J2.pin8
  Cniv40: U1.D6_(PWM), J2.pin7
  Cniv50: U1.D7, J2.pin6
  Cniv60: U1.D8, J2.pin5
  Cniv70: U1.D9_(PWM), J2.pin4
  Cniv80: U1.D10_(PWM), J2.pin3
  Cniv90/MOSI: U1.D11_(PWM), J2.pin2, J3.pin1
  Cniv100/MISO: U1.D12, J2.pin1, J3.pin5
  SCK: U1.D13, R1.Pin_1, J3.pin4
  Vtemp: U1.A0, J2.pin14
  Vtemp2: U1.A1, U2.Vo
  SDA: U1.A4, J1.pin2
  SCL: U1.A5, J1.pin3
  N1: LED1.cathode, R1.Pin_0

notes:
  Programmation ICSP
  Cuve
  Réseau
